# Fritzing sketch BLENotifier (saved by Fritzing 0.9.3b)

parts:
  Part1 = Arduino Pro Mini v13
  Part2 = Adafruit Bluefruit LE UART Friend [part_number="Adafruit #2479"]
  NEOPIXEL3 = Neopixel Strip -- White (60/m)
  D2 = Diode [package=diode-1n4148]
  D3 = Diode [package=diode-1n4148]
  R1 = Resistor [tolerance=±5% resistance=10k package="0805 [SMD]"]
  R2 = Resistor [tolerance=±5% resistance=10k package="0805 [SMD]"]
  C1 = Capacitor [package=cap-pth-small2]
  J1 = female pin header, 6 pins [form="♀ (female)"]
  R3 = Resistor [tolerance=±5% resistance=470 package="0805 [SMD]"]
  C2 = Electrolytic Capacitor [capacitance=0.1mF package="100 mil [THT, electrolytic]"]

nets:
  N1: Part1.DTR, Part2.RTS
  N2: Part1.D0/TX, Part2.RXI
  N3: Part1.D1/RX, Part2.TXO
  VCC: Part1.VCC, Part2.VIN
  GND: Part1.GND, Part2.GND, Part2.CTS, NEOPIXEL3.GND, C1.1, J1.pin6, C2.-
  N4: Part1.RAW, D2.A, J1.pin5
  N5: Part1.D7, R3.Pin_1
  N6: Part1.D5_PWM, R1.Pin_1
  N7: Part1.D4, R2.Pin_1, C1.2
  N8: NEOPIXEL3.+5V, R3.Pin_0
  N9: NEOPIXEL3.DI, D3.C, C2.+
  N10: D2.C, D3.A
  N11: R1.Pin_0, J1.pin3
  N12: R2.Pin_0, J1.pin4

notes:
  String of 10 RGB LEDs
  Diodes drop 1.2V from the battery 6V in order to get about 5V
  BLE Module
  Connection to the (modified) Blood pressure sensor
  1: GND
  2: +V BATT (6V)
  3: Pump
  4: Valve
  5: N/C
  6: N/C
  Arduino Pro Mini

custom parts:
  Adafruit Bluefruit LE UART Friend: The Bluefruit LE UART Friend makes it easy to add Bluetooth Low Energy connectivity to anything with a hardware or software serial port. We even have nice hardware flow control so you won't have to think about losing data. Connect to your Arduino or other microcontroller or even just a standard FTDI cable for debugging and testing.
  Neopixel Strip -- White (60/m): Neopixel Strip, White, 60 pixels per meter.
